# Fritzing sketch Soil_moisture_breadboard-0.8 (saved by Fritzing 0.9.3b)
circuit board: 7.13702cm x 6.26755cm
breadboards: 1

parts:
  Arduino_Pro-Mini = Arduino Pro Mini v13
  Status = LED - 5mm [color="Red (633nm)" package="5 mm [THT]"]
  R2 = Resistor [tolerance=±5% resistance=1k package=THT]
  SD_Card = Adafruit MicroSD card breakout board [part_number="Adafruit #254"]
  R5 = Resistor [tolerance=±5% resistance=10k package=THT]
  LoRa = Adafruit RFM9x LoRa Radio [part_number="Adafruit #3072 and #3073"]
  DS3231_RTC = Adafruit DS3231 [part_number="Adafruit #3013"]
  U1 = LIPO-2000mAh [package=lipo-2000]

nets:
  N1: Arduino_Pro-Mini.A4, DS3231_RTC.SDA
  N2: Arduino_Pro-Mini.A5, DS3231_RTC.SCL
  GND: Arduino_Pro-Mini.GND, R2.Pin_1, SD_Card.GND, LoRa.GND, DS3231_RTC.GND, U1.-
  VIN: Arduino_Pro-Mini.VCC, SD_Card.+3V3, R5.Pin_0, LoRa.VIN, DS3231_RTC.Vin, U1.+
  N3: Arduino_Pro-Mini.D13/SCK, SD_Card.CLK, LoRa.SCK
  N4: Arduino_Pro-Mini.D12/MISO, SD_Card.DO, LoRa.MISO
  N5: Arduino_Pro-Mini.D11_PWM/MOSI, SD_Card.DI, LoRa.MOSI
  N6: Arduino_Pro-Mini.D10_PWM/SS, SD_Card.CS
  N7: Arduino_Pro-Mini.D8, Status.anode
  N8: Arduino_Pro-Mini.D7, LoRa.EN
  N9: Arduino_Pro-Mini.D6_PWM, LoRa.RST
  N10: Arduino_Pro-Mini.D5_PWM, LoRa.CS
  N11: Arduino_Pro-Mini.D3_PWM, LoRa.DIO0
  N12: Arduino_Pro-Mini.D2, R5.Pin_1, DS3231_RTC.SQW
  N13: Status.cathode, R2.Pin_0

custom parts:
  Adafruit MicroSD card breakout board: Not just a simple breakout board, this microSD adapter goes the extra mile - designed for ease of use. Onboard 5v->3v regulator provides 150mA for power-hungry cards 3v level shifting means you can use this with ease on either 3v or 5v systems Uses a proper level shifting chip, not resistors: less problems, and faster read/write access Use 3 or 4 digital pins to read and write 2Gb+ of storage!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
  Adafruit RFM9x LoRa Radio: Sending data over long distances is like magic, and now you can be a magician with this range of powerful and easy-to-use radio modules. Sure, sometimes you want to talk to a computer (a good time to use WiFi) or perhaps communicate with a Phone (choose Bluetooth Low Energy!) but what if you want to send data very far? Most WiFi, Bluetooth, Zigbee and other wireless chipsets use 2.4GHz, which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
  Adafruit DS3231: The datasheet for the DS3231 explains that this part is an "Extremely Accurate I²C-Integrated RTC/TCXO/Crystal". And, hey, it does exactly what it says on the tin! This Real Time Clock (RTC) is the most precise you can get in a small, low power package. Most RTCs use an external 32kHz timing crystal that is used to keep time with low current draw. And that's all well and good, but those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
