# Fritzing sketch power_test (saved by Fritzing 0.9.3b)
circuit board: 8.46667cm x 5.64444cm
breadboards: 1

parts:
  RFM1 = RFM69HCW ISM Transciever
  Part1 = Arduino Pro Mini (3.3V)

nets:
  N1: RFM1.1_GND, Part1.GND
  N2: RFM1.2_MISO, Part1.MISO
  N3: RFM1.3_MOSI, Part1.MOSI
  N4: RFM1.4_SCK, Part1.SCK
  N5: RFM1.5_NSS_(CS), Part1.D5
  N6: RFM1.6_RESET, Part1.D6
  N7: RFM1.14_DIO0, Part1.D3

custom parts:
  RFM69HCW ISM Transciever: RF Transceiver by Hope RF. Well supported Arduino libraries are available. This ISM band transceiver is available in several frequencies e.g. 433MHz and 915MHz and it is also available in various feature versions.
