# Fritzing sketch soil_moisture_breadboard_1.0 (saved by Fritzing 0.9.3b)
circuit board: 8.46667cm x 5.64444cm
breadboards: 1

parts:
  ATMEGA_328 = Arduino Pro Mini v13
  RFM1 = RFM69HCW ISM Transciever
  LED2 = LED - 3mm [color="Green (570nm)" package="3 mm [THT]"]
  R1 = Resistor [tolerance=±2% resistance=10k package=THT]
  DS3231 = Adafruit DS3231 [part_number="Adafruit #3013"]
  TMP32 = TMP36 Temperature Sensor [package="TO92 [THT]"]

nets:
  VCC: ATMEGA_328.VCC, RFM1.13_3.3V, DS3231.Vin, TMP32.+Vs
  GND: ATMEGA_328.GND, RFM1.1_GND, RFM1.8_GND, RFM1.10_GND, R1.Pin_0, DS3231.GND, TMP32.GND
  N1: ATMEGA_328.A4, DS3231.SDA
  N2: ATMEGA_328.A5, DS3231.SCL
  N3: ATMEGA_328.A1, TMP32.Vout
  N4: ATMEGA_328.A0, DS3231.BAT
  N5: ATMEGA_328.D13/SCK, RFM1.4_SCK
  N6: ATMEGA_328.D12/MISO, RFM1.2_MISO
  N7: ATMEGA_328.D11_PWM/MOSI, RFM1.3_MOSI
  N8: ATMEGA_328.D9_PWM, LED2.anode
  N9: ATMEGA_328.D6_PWM, RFM1.6_RESET
  N10: ATMEGA_328.D5_PWM, RFM1.5_NSS_(CS)
  N11: ATMEGA_328.D3_PWM, RFM1.14_DIO0
  N12: LED2.cathode, R1.Pin_1

custom parts:
  RFM69HCW ISM Transciever: RF Transceiver by Hope RF. Well supported Arduino libraries are available. This ISM band transceiver is available in several frequencies e.g. 433MHz and 915MHz and it is also available in various feature versions.
  Adafruit DS3231: The datasheet for the DS3231 explains that this part is an "Extremely Accurate I²C-Integrated RTC/TCXO/Crystal". And, hey, it does exactly what it says on the tin! This Real Time Clock (RTC) is the most precise you can get in a small, low power package. Most RTCs use an external 32kHz timing crystal that is used to keep time with low current draw. And that's all well and good, but those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
