# Fritzing sketch power_latch_2 (saved by Fritzing 0.9.3b)
circuit board: 8.46667cm x 5.64444cm
breadboards: 1

parts:
  R1 = Resistor [tolerance=±5% resistance=10k package=THT]
  R3 = Resistor [tolerance=±5% resistance=220k package=THT]
  R4 = Resistor [tolerance=±5% resistance=10k package=THT]
  D1 = Rectifier Diode [part_number=1N4148 package="300 mil [THT]"]
  R5 = Resistor [tolerance=±5% resistance=100k package=THT]
  Q2 = NPN-Transistor [part_number=2N4401 package="TO92 [THT]"]
  Q3 = Basic FET P-Channel [part_number=FQP27P06 package="TO220 [THT]"]
  R6 = Resistor [tolerance=±5% resistance=100k package=THT]
  D2 = Rectifier Diode [part_number=1N4148 package="300 mil [THT]"]
  R7 = Resistor [tolerance=±5% resistance=10k package=THT]
  U1 = mystery part, 3 pins
  U2 = mystery part, 1 pin
  Q4 = PNP-Transistor [part_number=@N4403 package="TO92 [THT]"]

nets:
  N1: R1.Pin_0, U2.pin1
  3.3V: R1.Pin_1, Q3.source, R6.Pin_0, Q4.E, Q4.B
  N2: R3.Pin_0, R4.Pin_0, Q4.C
  GND: R3.Pin_1, R5.Pin_1, Q2.E, U1.pin3
  N3: R4.Pin_1, D1.anode
  N4: D1.cathode, R5.Pin_0, Q2.B, R7.Pin_0
  N5: Q2.C, Q3.gate, R6.Pin_1
  N6: Q3.drain, U1.pin1
  N7: D2.cathode, R7.Pin_1
  N8: D2.anode, U1.pin2
