# Fritzing sketch soil_moisture_breadboard_1.0 (saved by Fritzing 0.9.3b)
circuit board: 8.46667cm x 5.64444cm
breadboards: 1

parts:
  Part1 = Arduino Pro Mini v13
  RFM1 = RFM69HCW ISM Transciever
  LED2 = LED - 3mm [color="Green (570nm)" package="3 mm [THT]"]
  R1 = Resistor [tolerance=±2% resistance=10k package=THT]
  Part2 = Adafruit DS3231 [part_number="Adafruit #3013"]
  T1 = TMP36 Temperature Sensor [package="TO92 [THT]"]  # not connected

nets:
  GND: Part1.GND, RFM1.1_GND, RFM1.8_GND, RFM1.10_GND, R1.Pin_0, Part2.GND
  N1: Part1.A4, Part2.SDA
  N2: Part1.A5, Part2.SCL
  VCC: Part1.VCC, RFM1.13_3.3V, Part2.Vin
  N3: Part1.A0, Part2.BAT
  N4: Part1.D13/SCK, RFM1.4_SCK
  N5: Part1.D12/MISO, RFM1.2_MISO
  N6: Part1.D11_PWM/MOSI, RFM1.3_MOSI
  N7: Part1.D9_PWM, LED2.anode
  N8: Part1.D6_PWM, RFM1.6_RESET
  N9: Part1.D5_PWM, RFM1.5_NSS_(CS)
  N10: Part1.D3_PWM, RFM1.14_DIO0
  N11: LED2.cathode, R1.Pin_1

custom parts:
  RFM69HCW ISM Transciever: RF Transceiver by Hope RF. Well supported Arduino libraries are available. This ISM band transceiver is available in several frequencies e.g. 433MHz and 915MHz and it is also available in various feature versions.
  Adafruit DS3231: The datasheet for the DS3231 explains that this part is an "Extremely Accurate I²C-Integrated RTC/TCXO/Crystal". And, hey, it does exactly what it says on the tin! This Real Time Clock (RTC) is the most precise you can get in a small, low power package. Most RTCs use an external 32kHz timing crystal that is used to keep time with low current draw. And that's all well and good, but those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
